// Logisim project mips-like.circ as structural Verilog: 4 circuits, main circuit PROCESSADOR
module PROCESSADOR (
  output [31:0] \INSTRUÇÃO 
);

  wire button_1_out, clock_1_out, UC_jump, UC_regwrite, UC_ula_src;
  wire [1:0] UC_memtoreg;
  wire [7:0] PC_q_2;
  wire [31:0] adder_1_out, banco_de_registradores_1_r0_d, banco_de_registradores_1_r1_d, multiplexer_2_out,
       PC_q, ula_1_ula_out, undriven;

  Adder #(.width(32)) adder_1 (.a({PC_q[31:10], PC_q_2, PC_q[1:0]}), .b(32'h4), .out(adder_1_out));  // open: cin, cout
  Multiplexer #(.width(32)) multiplexer_1 (.in0(adder_1_out), .sel(UC_jump));  // open: in1, out, en
  Register #(.width(32)) PC (
    .Q({PC_q[31:10], PC_q_2, PC_q[1:0]}), .clk(clock_1_out), .clr(button_1_out));  // open: D, en
  Clock clock_1 (.out(clock_1_out));
  Button button_1 (.out(button_1_out));
  ROM #(.dataWidth(32)) rom_1 (.addr(PC_q_2), .data(\INSTRUÇÃO ));  // open: sel
  UC UC (
    .E3(\INSTRUÇÃO [31]), .E2(\INSTRUÇÃO [30]), .E1(\INSTRUÇÃO [29]), .E0(\INSTRUÇÃO [28]), .jump(UC_jump),
    .MemToReg(UC_memtoreg[0]), .ula_op0(UC_memtoreg[0]), .ula_op1(UC_memtoreg[1]), .ula_src(UC_ula_src),
    .RegWrite(UC_regwrite));  // open: RegDst, branch, MemRead, MemWrite
  BANCO_DE_REGISTRADORES banco_de_registradores_1 (
    .DATA_WRITE(ula_1_ula_out), .CLK(clock_1_out), .RW(\INSTRUÇÃO [27:24]),
    .R0_D(banco_de_registradores_1_r0_d), .R0(\INSTRUÇÃO [19:16]), .R1_D(banco_de_registradores_1_r1_d),
    .R1(\INSTRUÇÃO [23:20]), .RW_2(UC_regwrite), .RESET(button_1_out));
  Multiplexer #(.width(32)) multiplexer_2 (
    .in0(banco_de_registradores_1_r1_d), .in1(undriven), .out(multiplexer_2_out), .sel(UC_ula_src));  // open: en
  ULA ula_1 (
    .DATA_0(banco_de_registradores_1_r0_d), .DATA_1(multiplexer_2_out), .ULA_OUT(ula_1_ula_out),
    .ULA_OP(UC_memtoreg));
  RAM #(.dataWidth(32)) ram_1 ();  // open: addr, data, sel, clk, ld, clr

  // Notes on the sheet:
  //   REG_0
  //   REG_1
  //   REG_W
  //   contents of rom_1 (hex, n*v repeats v):
  //   120000
  //   DATA_W
  //   BANCO DE REGISTRADORES
  //   REG0_D
  //   REG1_D
  //   ULA
endmodule

module ULA (
  input  [31:0] DATA_0,
  input  [31:0] DATA_1,
  input  [1:0] ULA_OP,
  output [31:0] ULA_OUT
);

  wire comparator_1_eq, comparator_1_gt;
  wire [31:0] adder_1_out, multiplier_1_out, shifter_1_out;
  wire [31:31] or_1_out;

  Adder #(.width(32)) adder_1 (.a(DATA_0), .b(DATA_1), .out(adder_1_out));  // open: cin, cout
  Multiplier #(.width(32)) multiplier_1 (.a(DATA_0), .b(DATA_1), .out(multiplier_1_out));  // open: cin, cout
  Comparator #(.width(32), .mode("unsigned")) comparator_1 (
    .a(DATA_0), .b(DATA_1), .gt(comparator_1_gt), .eq(comparator_1_eq));  // open: lt
  or or_1 (or_1_out[31], comparator_1_gt, comparator_1_eq);
  Shifter #(.width(32)) shifter_1 (.in(DATA_0), .\dist (DATA_1[4:0]), .out(shifter_1_out));
  Multiplexer #(.select(2), .width(32), .enable("false")) multiplexer_1 (
    .in0(adder_1_out), .in1(multiplier_1_out), .in2({32{or_1_out[31]}}), .in3(shifter_1_out), .out(ULA_OUT),
    .sel(ULA_OP));
endmodule

module UC (
  input  E3,
  input  E2,
  input  E1,
  input  E0,
  output RegDst,
  output jump,
  output branch,
  output MemRead,
  output MemToReg,
  output ula_op0,
  output ula_op1,
  output MemWrite,
  output ula_src,
  output RegWrite
);

  wire and_1_out, and_2_out, and_5_out, and_6_out, and_7_out, and_8_out, and_9_out, and_10_out, and_11_out,
       and_12_out, and_13_out, and_14_out, and_15_out, not_2_out, not_3_out, not_4_out, not_5_out, not_6_out,
       not_7_out, not_8_out, not_9_out, not_10_out, not_11_out, not_12_out, not_13_out, not_14_out,
       not_15_out, not_16_out, not_17_out, not_18_out, not_19_out;

  not not_1 (RegDst, E2);
  and and_1 (and_1_out, E3, not_2_out);
  not not_2 (not_2_out, E0);
  and and_2 (and_2_out, E3, E2);
  and and_3 (MemRead, E2, not_3_out);
  not not_3 (not_3_out, E0);
  and and_4 (MemToReg, E2, not_4_out);
  not not_4 (not_4_out, E0);
  and and_5 (and_5_out, E1, not_5_out);
  not not_5 (not_5_out, E0);
  and and_6 (and_6_out, E3, not_6_out);
  not not_6 (not_6_out, E0);
  not not_7 (not_7_out, E3);
  not not_8 (not_8_out, E2);
  not not_9 (not_9_out, E1);
  not not_10 (not_10_out, E0);
  not not_11 (not_11_out, E3);
  and and_7 (and_7_out, not_11_out, not_12_out);
  not not_12 (not_12_out, E2);
  not not_13 (not_13_out, E2);
  and and_8 (and_8_out, not_13_out, not_14_out);
  not not_14 (not_14_out, E0);
  not not_15 (not_15_out, E3);
  and and_9 (and_9_out, not_15_out, E0);
  and and_10 (and_10_out, E1, E0);
  and and_11 (and_11_out, E3, E0);
  not not_16 (not_16_out, E3);
  and and_12 (and_12_out, not_16_out, not_17_out);
  not not_17 (not_17_out, E2);
  not not_18 (not_18_out, E3);
  and and_13 (and_13_out, not_18_out, not_19_out);
  not not_19 (not_19_out, E0);
  or or_1 (branch, and_1_out, and_2_out);
  or or_2 (ula_op0, and_5_out, and_6_out);
  and and_14 (and_14_out, not_7_out, not_8_out, not_9_out, E0);
  or or_3 (ula_op1, and_14_out, and_15_out);
  and and_15 (and_15_out, E3, not_10_out);
  or or_4 (MemWrite, and_7_out, and_8_out, and_9_out);
  or or_5 (ula_src, and_10_out, E2, and_11_out);
  or or_6 (RegWrite, and_12_out, and_13_out);

  assign jump = E3;
endmodule

module BANCO_DE_REGISTRADORES (
  input  [31:0] DATA_WRITE,
  input  [3:0] R0,
  input  CLK,
  input  [3:0] R1,
  input  [3:0] RW,
  input  RESET,
  input  RW_2,
  output [31:0] R0_D,
  output [31:0] R1_D
);

  wire demultiplexer_1_out0, demultiplexer_1_out1, demultiplexer_1_out2, demultiplexer_1_out3;
  wire [31:0] register_1_q, register_2_q, register_3_q, register_4_q;

  Demultiplexer #(.select(2), .enable("false")) demultiplexer_1 (
    .out0(demultiplexer_1_out0), .out1(demultiplexer_1_out1), .out2(demultiplexer_1_out2),
    .out3(demultiplexer_1_out3), .in(RW_2), .sel(RW[1:0]));
  Register #(.width(32)) register_1 (
    .D(DATA_WRITE), .en(demultiplexer_1_out0), .Q(register_1_q), .clk(CLK), .clr(RESET));
  Register #(.width(32)) register_2 (
    .D(DATA_WRITE), .en(demultiplexer_1_out1), .Q(register_2_q), .clk(CLK), .clr(RESET));
  Register #(.width(32)) register_3 (
    .D(DATA_WRITE), .en(demultiplexer_1_out2), .Q(register_3_q), .clk(CLK), .clr(RESET));
  Register #(.width(32)) register_4 (
    .D(DATA_WRITE), .en(demultiplexer_1_out3), .Q(register_4_q), .clk(CLK), .clr(RESET));
  Multiplexer #(.select(2), .width(32), .disabled(0), .enable("false")) multiplexer_1 (
    .in0(register_1_q), .in1(register_2_q), .in2(register_3_q), .in3(register_4_q), .out(R0_D), .sel(R0[1:0]));
  Multiplexer #(.select(2), .width(32), .enable("false")) multiplexer_2 (
    .in0(register_1_q), .in1(register_2_q), .in2(register_3_q), .in3(register_4_q), .out(R1_D), .sel(R1[1:0]));
endmodule
